// Digital circuit full_adder.dig as structural Verilog
module full_adder (
  input  a,
  input  b,
  input  vem,
  output vai,
  output soma
);

  wire and_1_out, and_2_out, and_3_out, and_4_out, and_5_out, and_6_out, and_7_out, not_1_out, not_2_out,
       not_3_out;

  not not_1 (not_1_out, a);
  not not_2 (not_2_out, b);
  not not_3 (not_3_out, vem);
  and and_1 (and_1_out, a, vem);
  and and_2 (and_2_out, a, b);
  and and_3 (and_3_out, b, vem);
  and and_4 (and_4_out, not_1_out, not_2_out, vem);
  and and_5 (and_5_out, not_1_out, b, not_3_out);
  and and_6 (and_6_out, a, not_2_out, not_3_out);
  and and_7 (and_7_out, a, b, vem);
  or or_1 (vai, and_1_out, and_2_out, and_3_out);
  or or_2 (soma, and_4_out, and_5_out, and_6_out, and_7_out);

  // Notes on the sheet:
  //   FullAdder
endmodule
