// Digital circuit regs.dig as structural Verilog
module regs (
  input  clk,
  input  [31:0] C,
  input  [3:0] b_2,
  input  [3:0] a_2,
  input  [3:0] c_2,
  input  wr,
  output [31:0] A,
  output [31:0] B
);

  wire decoder_1_out_1, decoder_1_out_2, decoder_1_out_3, decoder_1_out_4, decoder_1_out_5, decoder_1_out_6,
       decoder_1_out_7, decoder_1_out_8, decoder_1_out_9, decoder_1_out_10, decoder_1_out_11,
       decoder_1_out_12, decoder_1_out_13, decoder_1_out_14, decoder_1_out_15;
  wire [3:0] and_1_out, bitextender_1_out;
  wire [31:0] R1_q, R2_q, R3_q, R4_q, R5_q, R6_q, R7_q, R8_q, R9_q, R10_q, R11_q, R12_q, R13_q, R14_q, R15_q;

  BitExtender #(.inputBits(1), .outputBits(4)) bitextender_1 (.in(wr), .out(bitextender_1_out));
  assign and_1_out = c_2 & bitextender_1_out;  // And and_1, 4 bits wide
  Decoder #(.Selector_Bits(4)) decoder_1 (
    .sel(and_1_out), .out_1(decoder_1_out_1), .out_2(decoder_1_out_2), .out_3(decoder_1_out_3),
    .out_4(decoder_1_out_4), .out_5(decoder_1_out_5), .out_6(decoder_1_out_6), .out_7(decoder_1_out_7),
    .out_8(decoder_1_out_8), .out_9(decoder_1_out_9), .out_10(decoder_1_out_10), .out_11(decoder_1_out_11),
    .out_12(decoder_1_out_12), .out_13(decoder_1_out_13), .out_14(decoder_1_out_14), .out_15(decoder_1_out_15));  // open: out_0
  Register #(.Bits(32)) R1 (.D(C), .C(clk), .en(decoder_1_out_1), .Q(R1_q));
  Register #(.Bits(32)) R2 (.D(C), .C(clk), .en(decoder_1_out_2), .Q(R2_q));
  Register #(.Bits(32)) R3 (.D(C), .C(clk), .en(decoder_1_out_3), .Q(R3_q));
  Register #(.Bits(32)) R4 (.D(C), .C(clk), .en(decoder_1_out_4), .Q(R4_q));
  Register #(.Bits(32)) R5 (.D(C), .C(clk), .en(decoder_1_out_5), .Q(R5_q));
  Register #(.Bits(32)) R6 (.D(C), .C(clk), .en(decoder_1_out_6), .Q(R6_q));
  Register #(.Bits(32)) R7 (.D(C), .C(clk), .en(decoder_1_out_7), .Q(R7_q));
  Register #(.Bits(32)) R8 (.D(C), .C(clk), .en(decoder_1_out_8), .Q(R8_q));
  Register #(.Bits(32)) R9 (.D(C), .C(clk), .en(decoder_1_out_9), .Q(R9_q));
  Register #(.Bits(32)) R10 (.D(C), .C(clk), .en(decoder_1_out_10), .Q(R10_q));
  Register #(.Bits(32)) R11 (.D(C), .C(clk), .en(decoder_1_out_11), .Q(R11_q));
  Register #(.Bits(32)) R12 (.D(C), .C(clk), .en(decoder_1_out_12), .Q(R12_q));
  Register #(.Bits(32)) R13 (.D(C), .C(clk), .en(decoder_1_out_13), .Q(R13_q));
  Register #(.Bits(32)) R14 (.D(C), .C(clk), .en(decoder_1_out_14), .Q(R14_q));
  Register #(.Bits(32)) R15 (.D(C), .C(clk), .en(decoder_1_out_15), .Q(R15_q));
  Multiplexer #(.Selector_Bits(4), .Bits(32)) multiplexer_1 (
    .sel(a_2), .in_0({32{1'b0}}), .in_1(R1_q), .in_2(R2_q), .in_3(R3_q), .in_4(R4_q), .in_5(R5_q),
    .in_6(R6_q), .in_7(R7_q), .in_8(R8_q), .in_9(R9_q), .in_10(R10_q), .in_11(R11_q), .in_12(R12_q),
    .in_13(R13_q), .in_14(R14_q), .in_15(R15_q), .out(A));
  Multiplexer #(.Selector_Bits(4), .Bits(32)) multiplexer_2 (
    .sel(b_2), .in_0({32{1'b0}}), .in_1(R1_q), .in_2(R2_q), .in_3(R3_q), .in_4(R4_q), .in_5(R5_q),
    .in_6(R6_q), .in_7(R7_q), .in_8(R8_q), .in_9(R9_q), .in_10(R10_q), .in_11(R11_q), .in_12(R12_q),
    .in_13(R13_q), .in_14(R14_q), .in_15(R15_q), .out(B));

  // Notes on the sheet:
  //   R0
endmodule
