// Digital circuit somador_32bits.dig as structural Verilog
module somador_32bits (
  input  a_0,
  input  b_0,
  input  a_1,
  input  b_1,
  input  a_2,
  input  b_2,
  input  a_31,
  input  b_31,
  input  F,
  input  a_3,
  input  b_3,
  input  a_4,
  input  b_4,
  input  a_5,
  input  b_5,
  input  a_6,
  input  b_6,
  input  a_7,
  input  b_7,
  input  a_8,
  input  b_8,
  input  a_9,
  input  b_9,
  input  a_10,
  input  b_10,
  input  a_11,
  input  b_11,
  input  a_12,
  input  b_12,
  input  a_13,
  input  b_13,
  input  a_14,
  input  b_14,
  input  a_15,
  input  b_15,
  input  a_16,
  input  b_16,
  input  a_17,
  input  b_17,
  input  a_18,
  input  b_18,
  input  a_19,
  input  b_19,
  input  a_20,
  input  b_20,
  input  a_21,
  input  b_21,
  input  a_22,
  input  b_22,
  input  a_23,
  input  b_23,
  input  a_24,
  input  b_24,
  input  a_25,
  input  b_25,
  input  a_26,
  input  b_26,
  input  a_27,
  input  b_27,
  input  a_28,
  input  b_28,
  input  a_29,
  input  b_29,
  input  a_30,
  input  b_30,
  output r_0,
  output r_1,
  output r_2,
  output r_31,
  output overflow,
  output neg,
  output r_3,
  output r_4,
  output r_5,
  output r_6,
  output r_7,
  output r_8,
  output r_9,
  output r_10,
  output r_11,
  output r_12,
  output r_13,
  output r_14,
  output r_15,
  output r_16,
  output r_17,
  output r_18,
  output r_19,
  output r_20,
  output r_21,
  output r_22,
  output r_23,
  output r_24,
  output r_25,
  output r_26,
  output r_27,
  output r_28,
  output r_29,
  output r_30
);

  wire full_adder_1_vai, full_adder_2_vai, full_adder_3_vai, full_adder_4_vai, full_adder_5_vai,
       full_adder_6_vai, full_adder_7_vai, full_adder_8_vai, full_adder_9_vai, full_adder_10_vai,
       full_adder_11_vai, full_adder_12_vai, full_adder_13_vai, full_adder_14_vai, full_adder_15_vai,
       full_adder_16_vai, full_adder_17_vai, full_adder_18_vai, full_adder_19_vai, full_adder_20_vai,
       full_adder_21_vai, full_adder_22_vai, full_adder_23_vai, full_adder_24_vai, full_adder_25_vai,
       full_adder_26_vai, full_adder_27_vai, full_adder_28_vai, full_adder_29_vai, full_adder_30_vai,
       full_adder_31_vai, full_adder_32_vai, multiplexer_1_out, multiplexer_2_out, multiplexer_3_out,
       multiplexer_4_out, multiplexer_5_out, multiplexer_6_out, multiplexer_7_out, multiplexer_8_out,
       multiplexer_9_out, multiplexer_10_out, multiplexer_11_out, multiplexer_12_out, multiplexer_13_out,
       multiplexer_14_out, multiplexer_15_out, multiplexer_16_out, multiplexer_17_out, multiplexer_18_out,
       multiplexer_19_out, multiplexer_20_out, multiplexer_21_out, multiplexer_22_out, multiplexer_23_out,
       multiplexer_24_out, multiplexer_25_out, multiplexer_26_out, multiplexer_27_out, multiplexer_28_out,
       multiplexer_29_out, multiplexer_30_out, multiplexer_31_out, multiplexer_32_out, not_1_out, not_2_out,
       not_3_out, not_4_out, not_5_out, not_6_out, not_7_out, not_8_out, not_9_out, not_10_out, not_11_out,
       not_12_out, not_13_out, not_14_out, not_15_out, not_16_out, not_17_out, not_18_out, not_19_out,
       not_20_out, not_21_out, not_22_out, not_23_out, not_24_out, not_25_out, not_26_out, not_27_out,
       not_28_out, not_29_out, not_30_out, not_31_out, not_32_out;

  not not_1 (not_1_out, b_31);
  xor xor_1 (overflow, full_adder_2_vai, full_adder_1_vai);
  Multiplexer multiplexer_1 (.sel(F), .in_0(b_31), .in_1(not_1_out), .out(multiplexer_1_out));
  full_adder full_adder_1 (.a(a_31), .b(multiplexer_1_out), .vem(full_adder_2_vai), .vai(full_adder_1_vai), .soma(neg));
  not not_2 (not_2_out, b_30);
  Multiplexer multiplexer_2 (.sel(F), .in_0(b_30), .in_1(not_2_out), .out(multiplexer_2_out));
  full_adder full_adder_2 (
    .a(a_30), .b(multiplexer_2_out), .vem(full_adder_3_vai), .vai(full_adder_2_vai), .soma(r_30));
  not not_3 (not_3_out, b_29);
  Multiplexer multiplexer_3 (.sel(F), .in_0(b_29), .in_1(not_3_out), .out(multiplexer_3_out));
  full_adder full_adder_3 (
    .a(a_29), .b(multiplexer_3_out), .vem(full_adder_4_vai), .vai(full_adder_3_vai), .soma(r_29));
  not not_4 (not_4_out, b_28);
  Multiplexer multiplexer_4 (.sel(F), .in_0(b_28), .in_1(not_4_out), .out(multiplexer_4_out));
  full_adder full_adder_4 (
    .a(a_28), .b(multiplexer_4_out), .vem(full_adder_5_vai), .vai(full_adder_4_vai), .soma(r_28));
  not not_5 (not_5_out, b_27);
  Multiplexer multiplexer_5 (.sel(F), .in_0(b_27), .in_1(not_5_out), .out(multiplexer_5_out));
  full_adder full_adder_5 (
    .a(a_27), .b(multiplexer_5_out), .vem(full_adder_6_vai), .vai(full_adder_5_vai), .soma(r_27));
  not not_6 (not_6_out, b_26);
  Multiplexer multiplexer_6 (.sel(F), .in_0(b_26), .in_1(not_6_out), .out(multiplexer_6_out));
  full_adder full_adder_6 (
    .a(a_26), .b(multiplexer_6_out), .vem(full_adder_7_vai), .vai(full_adder_6_vai), .soma(r_26));
  not not_7 (not_7_out, b_25);
  Multiplexer multiplexer_7 (.sel(F), .in_0(b_25), .in_1(not_7_out), .out(multiplexer_7_out));
  full_adder full_adder_7 (
    .a(a_25), .b(multiplexer_7_out), .vem(full_adder_8_vai), .vai(full_adder_7_vai), .soma(r_25));
  not not_8 (not_8_out, b_24);
  Multiplexer multiplexer_8 (.sel(F), .in_0(b_24), .in_1(not_8_out), .out(multiplexer_8_out));
  full_adder full_adder_8 (
    .a(a_24), .b(multiplexer_8_out), .vem(full_adder_9_vai), .vai(full_adder_8_vai), .soma(r_24));
  not not_9 (not_9_out, b_23);
  Multiplexer multiplexer_9 (.sel(F), .in_0(b_23), .in_1(not_9_out), .out(multiplexer_9_out));
  full_adder full_adder_9 (
    .a(a_23), .b(multiplexer_9_out), .vem(full_adder_10_vai), .vai(full_adder_9_vai), .soma(r_23));
  not not_10 (not_10_out, b_22);
  Multiplexer multiplexer_10 (.sel(F), .in_0(b_22), .in_1(not_10_out), .out(multiplexer_10_out));
  full_adder full_adder_10 (
    .a(a_22), .b(multiplexer_10_out), .vem(full_adder_11_vai), .vai(full_adder_10_vai), .soma(r_22));
  not not_11 (not_11_out, b_21);
  Multiplexer multiplexer_11 (.sel(F), .in_0(b_21), .in_1(not_11_out), .out(multiplexer_11_out));
  full_adder full_adder_11 (
    .a(a_21), .b(multiplexer_11_out), .vem(full_adder_12_vai), .vai(full_adder_11_vai), .soma(r_21));
  not not_12 (not_12_out, b_20);
  Multiplexer multiplexer_12 (.sel(F), .in_0(b_20), .in_1(not_12_out), .out(multiplexer_12_out));
  full_adder full_adder_12 (
    .a(a_20), .b(multiplexer_12_out), .vem(full_adder_13_vai), .vai(full_adder_12_vai), .soma(r_20));
  not not_13 (not_13_out, b_19);
  Multiplexer multiplexer_13 (.sel(F), .in_0(b_19), .in_1(not_13_out), .out(multiplexer_13_out));
  full_adder full_adder_13 (
    .a(a_19), .b(multiplexer_13_out), .vem(full_adder_14_vai), .vai(full_adder_13_vai), .soma(r_19));
  not not_14 (not_14_out, b_18);
  Multiplexer multiplexer_14 (.sel(F), .in_0(b_18), .in_1(not_14_out), .out(multiplexer_14_out));
  full_adder full_adder_14 (
    .a(a_18), .b(multiplexer_14_out), .vem(full_adder_15_vai), .vai(full_adder_14_vai), .soma(r_18));
  not not_15 (not_15_out, b_17);
  Multiplexer multiplexer_15 (.sel(F), .in_0(b_17), .in_1(not_15_out), .out(multiplexer_15_out));
  full_adder full_adder_15 (
    .a(a_17), .b(multiplexer_15_out), .vem(full_adder_16_vai), .vai(full_adder_15_vai), .soma(r_17));
  not not_16 (not_16_out, b_16);
  Multiplexer multiplexer_16 (.sel(F), .in_0(b_16), .in_1(not_16_out), .out(multiplexer_16_out));
  full_adder full_adder_16 (
    .a(a_16), .b(multiplexer_16_out), .vem(full_adder_17_vai), .vai(full_adder_16_vai), .soma(r_16));
  not not_17 (not_17_out, b_15);
  Multiplexer multiplexer_17 (.sel(F), .in_0(b_15), .in_1(not_17_out), .out(multiplexer_17_out));
  full_adder full_adder_17 (
    .a(a_15), .b(multiplexer_17_out), .vem(full_adder_18_vai), .vai(full_adder_17_vai), .soma(r_15));
  not not_18 (not_18_out, b_14);
  Multiplexer multiplexer_18 (.sel(F), .in_0(b_14), .in_1(not_18_out), .out(multiplexer_18_out));
  full_adder full_adder_18 (
    .a(a_14), .b(multiplexer_18_out), .vem(full_adder_19_vai), .vai(full_adder_18_vai), .soma(r_14));
  not not_19 (not_19_out, b_13);
  Multiplexer multiplexer_19 (.sel(F), .in_0(b_13), .in_1(not_19_out), .out(multiplexer_19_out));
  full_adder full_adder_19 (
    .a(a_13), .b(multiplexer_19_out), .vem(full_adder_20_vai), .vai(full_adder_19_vai), .soma(r_13));
  not not_20 (not_20_out, b_12);
  Multiplexer multiplexer_20 (.sel(F), .in_0(b_12), .in_1(not_20_out), .out(multiplexer_20_out));
  full_adder full_adder_20 (
    .a(a_12), .b(multiplexer_20_out), .vem(full_adder_21_vai), .vai(full_adder_20_vai), .soma(r_12));
  not not_21 (not_21_out, b_11);
  Multiplexer multiplexer_21 (.sel(F), .in_0(b_11), .in_1(not_21_out), .out(multiplexer_21_out));
  full_adder full_adder_21 (
    .a(a_11), .b(multiplexer_21_out), .vem(full_adder_22_vai), .vai(full_adder_21_vai), .soma(r_11));
  not not_22 (not_22_out, b_10);
  Multiplexer multiplexer_22 (.sel(F), .in_0(b_10), .in_1(not_22_out), .out(multiplexer_22_out));
  full_adder full_adder_22 (
    .a(a_10), .b(multiplexer_22_out), .vem(full_adder_23_vai), .vai(full_adder_22_vai), .soma(r_10));
  not not_23 (not_23_out, b_9);
  Multiplexer multiplexer_23 (.sel(F), .in_0(b_9), .in_1(not_23_out), .out(multiplexer_23_out));
  full_adder full_adder_23 (
    .a(a_9), .b(multiplexer_23_out), .vem(full_adder_24_vai), .vai(full_adder_23_vai), .soma(r_9));
  not not_24 (not_24_out, b_8);
  Multiplexer multiplexer_24 (.sel(F), .in_0(b_8), .in_1(not_24_out), .out(multiplexer_24_out));
  full_adder full_adder_24 (
    .a(a_8), .b(multiplexer_24_out), .vem(full_adder_25_vai), .vai(full_adder_24_vai), .soma(r_8));
  not not_25 (not_25_out, b_7);
  Multiplexer multiplexer_25 (.sel(F), .in_0(b_7), .in_1(not_25_out), .out(multiplexer_25_out));
  full_adder full_adder_25 (
    .a(a_7), .b(multiplexer_25_out), .vem(full_adder_26_vai), .vai(full_adder_25_vai), .soma(r_7));
  not not_26 (not_26_out, b_6);
  Multiplexer multiplexer_26 (.sel(F), .in_0(b_6), .in_1(not_26_out), .out(multiplexer_26_out));
  full_adder full_adder_26 (
    .a(a_6), .b(multiplexer_26_out), .vem(full_adder_27_vai), .vai(full_adder_26_vai), .soma(r_6));
  not not_27 (not_27_out, b_5);
  Multiplexer multiplexer_27 (.sel(F), .in_0(b_5), .in_1(not_27_out), .out(multiplexer_27_out));
  full_adder full_adder_27 (
    .a(a_5), .b(multiplexer_27_out), .vem(full_adder_28_vai), .vai(full_adder_27_vai), .soma(r_5));
  not not_28 (not_28_out, b_4);
  Multiplexer multiplexer_28 (.sel(F), .in_0(b_4), .in_1(not_28_out), .out(multiplexer_28_out));
  full_adder full_adder_28 (
    .a(a_4), .b(multiplexer_28_out), .vem(full_adder_29_vai), .vai(full_adder_28_vai), .soma(r_4));
  not not_29 (not_29_out, b_3);
  Multiplexer multiplexer_29 (.sel(F), .in_0(b_3), .in_1(not_29_out), .out(multiplexer_29_out));
  full_adder full_adder_29 (
    .a(a_3), .b(multiplexer_29_out), .vem(full_adder_30_vai), .vai(full_adder_29_vai), .soma(r_3));
  not not_30 (not_30_out, b_2);
  Multiplexer multiplexer_30 (.sel(F), .in_0(b_2), .in_1(not_30_out), .out(multiplexer_30_out));
  full_adder full_adder_30 (
    .a(a_2), .b(multiplexer_30_out), .vem(full_adder_31_vai), .vai(full_adder_30_vai), .soma(r_2));
  not not_31 (not_31_out, b_1);
  Multiplexer multiplexer_31 (.sel(F), .in_0(b_1), .in_1(not_31_out), .out(multiplexer_31_out));
  full_adder full_adder_31 (
    .a(a_1), .b(multiplexer_31_out), .vem(full_adder_32_vai), .vai(full_adder_31_vai), .soma(r_1));
  not not_32 (not_32_out, b_0);
  Multiplexer multiplexer_32 (.sel(F), .in_0(b_0), .in_1(not_32_out), .out(multiplexer_32_out));
  full_adder full_adder_32 (.a(a_0), .b(multiplexer_32_out), .vem(F), .vai(full_adder_32_vai), .soma(r_0));

  assign r_31 = neg;
endmodule
