// Digital circuit system.dig as structural Verilog
module system (
  input  clock
);

  wire and_1_out, and_2_out, not_1_out, not_2_out, not_3_out;
  wire [3:0] MI_d_2, MI_d_3, MI_d_4, MI_d_5;
  wire [6:0] CONTROLE_d;
  wire [15:0] MI_d;
  wire [23:0] PC_q;
  wire [31:0] add_1_s, bitextender_1_out, DADOS_d, multiplexer_1_out, multiplexer_2_out, regs_1_a, regs_1_b,
       ula_32bits_1_r;
  wire [31:24] PC_q_2;

  D_FF #(.Bits(32)) PC (.D(add_1_s), .C(clock), .Q({PC_q_2, PC_q}));  // open: nQ
  Add #(.Bits(32)) add_1 (.a(32'h1), .b({PC_q_2, PC_q}), .c_i(1'b0), .s(add_1_s));  // open: c_o
  ROM #(.AddrBits(24), .isProgramMemory("true"), .Bits(32)) MI (
    .A(PC_q), .sel(1'b1), .D({MI_d_5, MI_d_4, MI_d_3, MI_d_2, MI_d}));
  ROM #(.AddrBits(4), .Bits(7)) CONTROLE (.A(MI_d_5), .sel(1'b1), .D(CONTROLE_d));
  BitExtender #(.inputBits(16), .outputBits(32)) bitextender_1 (.in(MI_d), .out(bitextender_1_out));
  regs regs_1 (
    .clk(clock), .a_2(MI_d_4), .b_2(MI_d_3), .c_2(MI_d_2), .C(multiplexer_2_out), .A(regs_1_a), .B(regs_1_b),
    .wr(CONTROLE_d[1]));
  Multiplexer #(.Bits(32)) multiplexer_1 (
    .sel(CONTROLE_d[3]), .in_0(regs_1_b), .in_1(bitextender_1_out), .out(multiplexer_1_out));
  ula_32bits ula_32bits_1 (
    .R(ula_32bits_1_r), .F(CONTROLE_d[6:4]), .A(regs_1_a), .B(multiplexer_1_out));  // open: overflow, zero, neg
  Multiplexer #(.Bits(32)) multiplexer_2 (
    .sel(CONTROLE_d[2]), .in_0(ula_32bits_1_r), .in_1(DADOS_d), .out(multiplexer_2_out));
  RAMDualPort #(.AddrBits(24), .Bits(32)) DADOS (
    .A(ula_32bits_1_r[23:0]), .Din(regs_1_b), .str(and_1_out), .C(clock), .ld(not_3_out), .D(DADOS_d));
  and and_1 (and_1_out, not_3_out, CONTROLE_d[0]);
  not not_1 (not_1_out, MI_d_5[2]);
  not not_2 (not_2_out, MI_d_5[0]);
  not not_3 (not_3_out, and_2_out);
  and and_2 (and_2_out, ula_32bits_1_r[24], ula_32bits_1_r[25], ula_32bits_1_r[26], ula_32bits_1_r[27], ula_32bits_1_r[28], ula_32bits_1_r[29], ula_32bits_1_r[30], ula_32bits_1_r[31], not_2_out, MI_d_5[1], not_1_out, MI_d_5[3]);
  Terminal #(.termWidth(80), .termHeight(24)) TERMINAL (.D(regs_1_b), .C(clock), .en(and_2_out));

  // Notes on the sheet:
  //   PC + 1
  //   contents of MI (hex, n*v repeats v):
  //   8001cafe,8002dead,1230000,8006000c,a6300000,a6200001,96070001
  //   ,800dff00,80070041,ad700000
  //   CONTROLE
  //   contents of CONTROLE (hex, n*v repeats v):
  //   2,12,22,32,42,0,0,0,a,e,9
  //   wrReg
  //   selB
  //   selC
  //   aluFunc
  //   ULA
  //   MD
  //   wrMem
  //   TERMINAL
endmodule
